# Fritzing sketch cxemaPaneli (saved by Fritzing 0.9.2b)
circuit board: 8.46667cm x 5.64444cm
breadboards: 1

parts:
  Часть1 = Arduino Uno (Rev3)
  R1 = Resistor [tolerance=±5% resistance=47k part_number=Вольметр package=THT]
  R2 = Resistor [tolerance=±5% resistance=10k package=THT]
  M1 = DC Motor [part_number="Спидометр датчик"]
  R3 = Resistor [tolerance=±5% resistance=10k package=THT]
  M2 = DC Motor [part_number="Тахометр датчик"]
  R4 = Resistor [tolerance=±5% resistance=10k package=THT]
  R6 = Resistor [tolerance=±5% resistance=220 part_number="Делитель напряжений" package=THT]
  R7 = Resistor [tolerance=±5% resistance=220 package=THT]
  R8 = Resistor [tolerance=±5% resistance=220 package=THT]
  S1 = Pushbutton [part_number="Левый сигнал" package=THT]
  S2 = Pushbutton [part_number="Правый сигнал" package=THT]
  S3 = Pushbutton [part_number="Дальний свет" package=THT]
  S4 = Pushbutton [part_number=Нейтраль package=THT]
  S5 = Pushbutton [part_number=Подножка package=THT]
  S6 = Pushbutton [part_number="Давление масла" package=THT]
  R9 = Resistor [tolerance=±5% resistance=10k package=THT]
  R10 = Resistor [tolerance=±5% resistance=10k package=THT]
  R11 = Resistor [tolerance=±5% resistance=10k package=THT]
  R12 = Resistor [tolerance=±5% resistance=10k package=THT]
  R13 = Resistor [tolerance=±5% resistance=10k package=THT]
  R14 = Resistor [tolerance=±5% resistance=10k package=THT]
  Зажигание = Round Pushbutton
  Управляющее_реле = RELAY [package=relay-jzc]
  акум = Power plug
  Понижающий_стабилизатор = Voltage Regulator - 5V [package="TO220 [THT]"]
  D1 = Rectifier Diode [part_number=1N4001 package="300 mil [THT]"]
  R15 = Resistor [tolerance=±5% resistance=14k package=THT]
  R16 = Resistor [tolerance=±5% resistance=10k package=THT]
  R5 = Trimmer Potentiometer [maximum_resistance=10kΩ part_number="Датчик топлива" package=THT]
  R17 = Trimmer Potentiometer [maximum_resistance=10kΩ part_number="Датчик температуры" package=THT]
  R18 = Resistor [tolerance=±5% resistance=220 package=THT]
  R19 = Resistor [tolerance=±5% resistance=10k package=THT]
  R20 = Resistor [tolerance=±5% resistance=10k package=THT]
  R21 = Resistor [tolerance=±5% resistance=10k package=THT]

nets:
  N1: Часть1.A0, R1.Pin_0, R2.Pin_1
  N2: Часть1.A1, R6.Pin_0, R7.Pin_0, R8.Pin_0, R5.leg1
  N3: Часть1.A2, R18.Pin_1, R19.Pin_0, R20.Pin_0, R21.Pin_0
  N4: Часть1.D8, S5.leg0, R10.Pin_0
  N5: Часть1.D9_PWM, S6.leg0, R12.Pin_0
  N6: Часть1.D12/MISO, R15.Pin_0, R16.Pin_0
  GND: Часть1.GND, R2.Pin_0, M1.pin_2, R3.Pin_0, M2.pin_2, R4.Pin_0, Управляющее_реле.COIL1, акум.GND, Понижающий_стабилизатор.GND, R16.Pin_1, R5.leg2, R17.leg2
  N7: Часть1.D2, M1.pin_1, R3.Pin_1
  N8: Часть1.D3_PWM, M2.pin_1, R4.Pin_1
  N9: Часть1.D4, S1.leg0, R13.Pin_0
  N10: Часть1.D5_PWM, S2.leg0, R14.Pin_0
  N11: Часть1.D6_PWM, S3.leg0, R11.Pin_0
  N12: Часть1.D7, S4.leg0, R9.Pin_0
  N13: Часть1.5V, R6.Pin_1, R7.Pin_1, R8.Pin_1, R19.Pin_1, R20.Pin_1, R21.Pin_1
  12V: R1.Pin_1
  5V: S1.leg1, S2.leg1, S3.leg1, S4.leg1, S5.leg1, S6.leg1
  N14: R9.Pin_1, R10.Pin_1, R11.Pin_1, R12.Pin_1, R13.Pin_1, R14.Pin_1
  N15: Зажигание.leg0, Управляющее_реле.NO, акум.VCC
  N16: Зажигание.leg1, D1.anode, R15.Pin_1
  N17: Управляющее_реле.COIL2, Понижающий_стабилизатор.output_voltage
  N18: Управляющее_реле.MAIN, Понижающий_стабилизатор.input_voltage, D1.cathode
  N19: R17.leg1, R18.Pin_0

// code stored in the sketch: Untitled2.ino

