# Fritzing sketch макеткаPaneli (saved by Fritzing 0.9.2b)
perfboards: 1

parts:
  R1 = Resistor [tolerance=±5% resistance=10k package=THT]
  R2 = Resistor [tolerance=±5% resistance=10k package=THT]
  R3 = Resistor [tolerance=±5% resistance=10k package=THT]
  R4 = Resistor [tolerance=±5% resistance=10k package=THT]
  R5 = Resistor [tolerance=±5% resistance=10k package=THT]
  R6 = Resistor [tolerance=±5% resistance=10k package=THT]
  R7 = Resistor [tolerance=±5% resistance=10k package=THT]
  R8 = Resistor [tolerance=±5% resistance=10k package=THT]
  R9 = Resistor [tolerance=±5% resistance=10k package=THT]
  R10 = Resistor [tolerance=±5% resistance=10k package=THT]
  R11 = Resistor [tolerance=±5% resistance=10k package=THT]
  R12 = Resistor [tolerance=±5% resistance=220 package=THT]
  Часть1 = Arduino Uno (Rev3) - ICSP
  D1 = Diode [package=diode-1n4001]
  U1 = Voltage Regulator - 5V [package="TO220 [THT]"]
  R13 = Resistor [tolerance=±5% resistance=10k package=THT]
  R14 = Resistor [tolerance=±5% resistance=13k package=THT]
  R15 = Resistor [tolerance=±5% resistance=1k package=THT]
  R16 = Resistor [tolerance=±5% resistance=10k package=THT]
  R17 = Resistor [tolerance=±5% resistance=47k package=THT]
  R18 = Resistor [tolerance=±5% resistance=220 package=THT]
  R19 = Resistor [tolerance=±5% resistance=220 package=THT]
  R20 = Resistor [tolerance=±5% resistance=220 package=THT]
  S1 = Pushbutton [part_number=зажигание package=THT]
  Power_plug1 = Power plug
  J1 = shrouded pin header, 10 pins [form="♂ (shrouded male)"]
  J2 = shrouded pin header, 10 pins [form="♂ (shrouded male)"]
  U2 = RELAY [package=relay-g5q]

nets:
  GND: R1.Pin_0, R2.Pin_0, R3.Pin_0, R4.Pin_0, R5.Pin_0, R6.Pin_0, R7.Pin_0, R8.Pin_0, Часть1.GND, U1.GND, R13.Pin_0, R16.Pin_0, Power_plug1.GND, U2.COIL1
  N1: R1.Pin_1, Часть1.D9_PWM, J1.pin5
  N2: R2.Pin_1, Часть1.D8, J1.pin4
  N3: R3.Pin_1, Часть1.D7, J1.pin3
  N4: R4.Pin_1, Часть1.D6_PWM, J1.pin2
  N5: R5.Pin_1, Часть1.D5_PWM, J1.pin1
  N6: R6.Pin_1, Часть1.D4, J1.pin10
  N7: R7.Pin_1, Часть1.D3_PWM, J1.pin9
  N8: R8.Pin_1, Часть1.D2, J1.pin8
  N9: R9.Pin_0, R10.Pin_0, R11.Pin_0, R12.Pin_1, Часть1.A2
  N10: R9.Pin_1, R10.Pin_1, R11.Pin_1, Часть1.5V, U1.output_voltage, R18.Pin_1, R19.Pin_1, R20.Pin_1, U2.COIL2
  N11: R12.Pin_0, J2.pin4
  N12: Часть1.A0, R16.Pin_1, R17.Pin_0
  N13: Часть1.A1, R18.Pin_0, R19.Pin_0, R20.Pin_0, J2.pin5
  N14: Часть1.ICSP_MISO, Часть1.D12/MISO, R13.Pin_1, R15.Pin_0
  N15: Часть1.D13/SCK, J2.pin1
  N16: D1.A, R14.Pin_1, S1.leg0, J2.pin2
  N17: D1.C, U1.input_voltage, U2.MAIN
  N18: R14.Pin_0, R15.Pin_1
  N19: R17.Pin_1, J2.pin8
  N20: Power_plug1.VCC, U2.NO
